# Fritzing sketch circuit (saved by Fritzing 1.0.6)

parts:
  A1 = MD30C
  A3 = Raspberry Pi 5
  BAT1 = 24 battery [package=battery]  # not connected
  J1 = STM32 Nucleo boards  # not connected
  A4 = MD30C

nets:
  N1: A1.pin_19, A3.GPIO16
  N2: A1.pin_20, A3.GPIO20
  N3: A3.GPIO19, A4.pin_19
  N4: A3.GPIO26, A4.pin_20

custom parts:
  Raspberry Pi 5: The RPi5, a faster version of the awesome Raspberry Pi4B ARM Board with 40 pin gpio.
  24 battery: 24V lead acid type battery, like the Husqvarna YTH2448 12V 35AH battery. This is the mini version 1/4 the size of the actual battery to be closer to typical breadboard parts (around 2in wide rathher than 7in). The pads in pcb are sized to accomidate up to 14ga wire (as these batterys will deliver high currents.)
