# Fritzing sketch circuit (saved by Fritzing 1.0.6)
breadboards: 1

parts:
  A1 = MD30C
  A3 = Raspberry Pi 5  # not connected
  A4 = MD30C
  Part1 = Adafruit BNO085 9-DOF Orientation IMU Fusion [part_number="Addfruit #4754"]
  Part2 = Adafruit Ultimate GPS HAT [part_number="Adafruit #2324"]
  M2 = DC Motor [voltage_(max)=12V voltage_(min)=3V]
  BAT2 = 12 battery [package=battery]
  BAT3 = 12 battery [package=battery]
  M1 = DC Motor [voltage_(max)=12V voltage_(min)=3V]
  HC-SR04_Sensor_1 = HC-SR04 Ultrasonic Distance Sensor  # not connected
  HC-SR04_Sensor_2 = HC-SR04 Ultrasonic Distance Sensor  # not connected
  HC-SR04_Sensor_3 = HC-SR04 Ultrasonic Distance Sensor  # not connected
  HC-SR04_Sensor_4 = HC-SR04 Ultrasonic Distance Sensor
  Part3 = Adafruit T-Cobbler Plus [part_number="Adafruit #1989 and #2028"]
  RevA1 = BeagleY-AI  # not connected
  Part4 = Adafruit TCA9548A  # not connected

nets:
  N1: A1.pin_1, BAT2.+
  GND: A1.pin_2, A1.pin_3, A4.pin_2, A4.pin_3, Part1.GND, Part2.GND, BAT2.-, BAT3.-, HC-SR04_Sensor_4.GND, Part3.GND
  N2: A1.pin_4, Part1.SDA/MISO/TX, Part3.GPIO13, Part3.GPIO20
  N3: A1.pin_5, Part3.GPIO5
  N4: A1.pin_19, M2.pin_1
  N5: A1.pin_20, M2.pin_2
  N6: A4.pin_1, BAT3.+
  N7: A4.pin_4, Part1.SCL/SCK/RX, Part3.GPIO26, Part3.GPIO12
  N8: A4.pin_5, Part3.GPIO19
  N9: A4.pin_19, M1.pin_1
  N10: A4.pin_20, M1.pin_2
  VCC: Part1.VCC, Part1.PS1, Part2.3.3V, Part3.+3.3V
  N11: Part2.TXD, Part3.TXD
  N12: Part2.RXD, Part3.RXD
  N13: Part2.GPIO4, Part3.GPIO4
  VCC_2: HC-SR04_Sensor_4.VCC, Part3.+5V

custom parts:
  Raspberry Pi 5: The RPi5, a faster version of the awesome Raspberry Pi4B ARM Board with 40 pin gpio.
  Adafruit Ultimate GPS HAT: It's 10PM, do you know where your Raspberry Pi is? If you had this GPS HAT, you would! This new HAT from Adafruit adds our celebrated Ultimate GPS on it, so you can add precision time and location to your Raspberry Pi Model A+, B+, or Pi 2. Does not work with the Pi 3 at this time Here's the low-down on the GPS module: -165 dBm sensitivity, 10 Hz updates, 66 channels Only 20mA current draw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
  12 battery: 12V lead acid type battery, like the Husqvarna YTH2448 12V 35AH battery. This is the mini version 1/4 the size of the actual battery to be closer to typical breadboard parts (around 2in wide rathher than 7in). The pads in pcb are sized to accomidate up to 14ga wire (as these batterys will deliver high currents.)
  Adafruit T-Cobbler Plus: The Raspberry Pi has landed on the Maker World like a 40-GPIO pinned, quad-USB ported, credit card sized bomb of DIY joy. And while you can use most of our great Model B accessories by hooking up our downgrade cable, its probably a good time to upgrade your set up and accessorize using all of the 40 pins. That's why we now carry the Assembled Adafruit Pi T-Cobbler Plus - Breakout + Cable for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
  Adafruit TCA9548A: You just found the perfect I2C sensor, and you want to wire up two or three or more of them to your Arduino when you realize "Uh oh, this chip has a fixed I2C address, and from what I know about I2C, you cannot have two devices with the same address on the same SDA/SCL pins!" Are you out of luck? You would be, if you didn't have this ultra-cool TCA9548A 1-to-8 I2C multiplexer! Finally, a way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
